# Fritzing sketch coffee_tree_monitor_fona_dev (saved by Fritzing 0.9.3b)
breadboards: 2

parts:
  C1 = Electrolytic Capacitor [capacitance=10µF voltage=50V package="100 mil [THT, electrolytic]"]
  C2 = Ceramic Capacitor [capacitance=0.1µF voltage=50V package="100 mil [THT, multilayer]"]
  Part1 = Adafruit Feather 32u4 FONA [part_number="Adafruit #3027"]
  Part3 = Adafruit BMP180
  Part4 = Adafruit TSL2561 [part_number="Adafruit #439"]
  ZS-042_RTC1 = ZS-042 RTC Module  # not connected
  Part5 = MicroSD Card Module

nets:
  +5V: C1.-, C2.0, Part1.11, Part3.+5V, Part4.VIN
  GND: C1.+, C2.1, Part1.GND, Part3.GND, Part4.GND, Part5.GND
  N1: Part1.KEY, Part1.12
  N2: Part1.MISO, Part5.MISO
  N3: Part1.MOSI, Part5.MOSI
  N4: Part1.SCK, Part5.SCK
  +3V3: Part1.+3V3, Part5.VCC
  N5: Part1.10, Part5.CS
  N6: Part1.3, Part3.SCL, Part4.SCL
  N7: Part1.2, Part3.SDA, Part4.SDA

custom parts:
  Adafruit Feather 32u4 FONA: This is the Adafruit Feather 32u4 FONA - our take on an 'all-in-one' Arduino-compatible + audio/sms/data capable cellular with built in USB and battery charging. Its an Adafruit Feather 32u4 with a FONA800 module, ready to rock! We have other boards and accessories in the Feather family, check'em out here. At the Feather 32u4's heart is at ATmega32u4 clocked at 8 MHz and at 3.3V logic, a chip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
  Adafruit BMP180: This precision sensor from Bosch is the best low-cost sensing solution for measuring barometric pressure and temperature. Because pressure changes with altitude you can also use it as an altimeter! The sensor is soldered onto a PCB with a 3.3V regulator, I2C level shifter and pull-up resistors on the I2C pins. The BMP180 is the next-generation of sensors from Bosch, and replaces the BMP085.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
  Adafruit TSL2561: The TSL2561 luminosity sensor is an advanced digital light sensor, ideal for use in a wide range of light situations. Compared to low cost CdS cells, this sensor is more precise, allowing for exact lux calculations and can be configured for different gain/timing ranges to detect light ranges from up to 0.1 - 40,000+ Lux on the fly. The best part of this sensor is that it contains both infrared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
